// Logisim project HW3#2c.circ as structural Verilog: 1 circuit, main circuit main
module main (
  input  a,
  input  b,
  output out_3,
  output y2,
  output out_5
);

  or y1 (out_3, a, b);
  and and_1 (y2, a, b);
  and y3 (out_5, a, b);
endmodule
