// Logisim project LogisimSchematic.circ as structural Verilog: 1 circuit, main circuit main
module main (
  input  Clk,
  input  Traffic,
  input  _1,
  output Q2,
  output Q1,
  output Q0,
  output R,
  output Y,
  output G,
  output R_2,
  output Y_2,
  output G_2
);

  wire and_1_out, and_2_out, and_3_out, and_4_out, and_6_out, and_7_out, and_8_out, and_9_out, j_k_ff_1_qn,
       j_k_ff_2_qn, j_k_ff_3_qn, or_1_out;

  and and_1 (and_1_out, Q1, Q0);
  J_K_Flip_Flop j_k_ff_1 (
    .J(and_1_out), .clk(Clk), .K(and_1_out), .Q(Q2), .Qn(j_k_ff_1_qn));  // open: preset, en, reset
  J_K_Flip_Flop j_k_ff_2 (.J(Q0), .clk(Clk), .K(Q0), .Q(Q1), .Qn(j_k_ff_2_qn));  // open: preset, en, reset
  or or_1 (or_1_out, Q2, Q1, Traffic);
  J_K_Flip_Flop j_k_ff_3 (.J(or_1_out), .clk(Clk), .K(_1), .Q(Q0), .Qn(j_k_ff_3_qn));  // open: preset, en, reset
  and and_2 (and_2_out, Q1, Q0);
  or or_2 (R, and_2_out, Q2);
  and and_3 (and_3_out, j_k_ff_1_qn, j_k_ff_2_qn, Q0);
  and and_4 (and_4_out, j_k_ff_1_qn, Q1, j_k_ff_3_qn);
  and and_5 (G, j_k_ff_3_qn, j_k_ff_2_qn, j_k_ff_1_qn);
  and and_6 (and_6_out, j_k_ff_1_qn, j_k_ff_2_qn);
  or or_3 (R_2, and_6_out, and_7_out);
  and and_7 (and_7_out, j_k_ff_1_qn, j_k_ff_3_qn);
  or or_4 (Y_2, and_8_out, and_9_out);
  and and_8 (and_8_out, j_k_ff_1_qn, Q1, Q0);
  and and_9 (and_9_out, Q2, j_k_ff_2_qn);
  or or_5 (Y, and_3_out, and_4_out);
  and and_10 (G_2, Q1, Q2);

  // Notes on the sheet:
  //   State
  //   HIghway
  //   Gravel
endmodule
