// Logisim project LogisimSchematic.circ as structural Verilog: 1 circuit, main circuit main
module main (
  input  Clk,
  input  START,
  output Q2,
  output Q1,
  output Q0,
  output OUTPUT
);

  wire and_1_out, j_k_ff_1_qn, j_k_ff_2_qn, or_1_out, or_3_out;

  and and_1 (and_1_out, Q0, Q1);
  J_K_Flip_Flop j_k_ff_1 (
    .J(and_1_out), .clk(Clk), .K(Q1), .Q(Q2), .Qn(j_k_ff_1_qn), .en(START));  // open: preset, reset
  or or_1 (or_1_out, Q2, Q0);
  or or_2 (OUTPUT, Q1, Q0, Q2);
  J_K_Flip_Flop j_k_ff_2 (
    .J(Q0), .clk(Clk), .K(or_1_out), .Q(Q1), .Qn(j_k_ff_2_qn), .en(START));  // open: preset, reset
  or or_3 (or_3_out, j_k_ff_2_qn, j_k_ff_1_qn);
  J_K_Flip_Flop j_k_ff_3 (.J(or_3_out), .clk(Clk), .K(Q0), .Q(Q0), .en(START));  // open: Qn, preset, reset
endmodule
