// Logisim project HW.circ as structural Verilog: 1 circuit, main circuit main
module main (
  input  in_1,
  input  in_2,
  input  in_3,
  output out_4,
  output out_5,
  output out_6
);

  wire and_1_out, and_2_out, and_3_out, j_k_ff_1_qn, j_k_ff_2_qn, j_k_ff_3_qn;

  and and_1 (and_1_out, out_5, out_6);
  J_K_Flip_Flop j_k_ff_1 (
    .J(and_1_out), .clk(in_1), .K(and_1_out), .Q(out_4), .Qn(j_k_ff_1_qn), .en(in_3), .reset(in_2));  // open: preset
  J_K_Flip_Flop j_k_ff_2 (
    .J(out_6), .clk(in_1), .K(out_6), .Q(out_5), .Qn(j_k_ff_2_qn), .en(in_3), .reset(in_2));  // open: preset
  and and_2 (and_2_out, j_k_ff_1_qn, j_k_ff_2_qn);
  and and_3 (and_3_out, and_2_out, j_k_ff_3_qn);
  J_K_Flip_Flop j_k_ff_3 (
    .J(and_2_out), .clk(in_1), .K(and_3_out), .Q(out_6), .Qn(j_k_ff_3_qn), .en(in_3), .reset(in_2));  // open: preset
endmodule
