// Logisim project HW2#4.9.circ as structural Verilog: 1 circuit, main circuit main
module main (
  input  A,
  input  B,
  input  C,
  input  D,
  output out_5,
  output out_6,
  output out_7,
  output out_8,
  output out_9,
  output out_10,
  output out_11,
  output out_12,
  output out_13,
  output out_14,
  output out_15,
  output out_16,
  output out_17,
  output out_18,
  output out_19,
  output out_20,
  output out_21,
  output out_22,
  output out_23,
  output out_24,
  output out_25
);

  wire and_1_out, and_2_out, and_3_out, and_4_out, and_5_out, and_6_out, and_7_out, and_8_out, and_9_out,
       and_10_out, and_11_out, and_12_out, and_13_out, and_14_out, and_15_out, and_16_out, not_1_out,
       not_2_out, not_3_out, not_4_out;

  not not_1 (not_1_out, A);
  not not_2 (not_2_out, B);
  not not_3 (not_3_out, C);
  not not_4 (not_4_out, D);
  and and_1 (and_1_out, not_1_out, C);
  and and_2 (and_2_out, not_1_out, B, D);
  and and_3 (and_3_out, A, not_2_out, not_3_out);
  and and_4 (and_4_out, not_1_out, not_2_out, not_4_out);
  and and_5 (and_5_out, not_1_out, not_2_out);
  and and_6 (and_6_out, not_1_out, C, D);
  and and_7 (and_7_out, not_2_out, not_3_out);
  and and_8 (and_8_out, not_1_out, not_3_out, not_4_out);
  and and_9 (and_9_out, not_1_out, D);
  and and_10 (and_10_out, not_1_out, B);
  and and_11 (and_11_out, not_1_out, B, not_3_out, D);
  and and_12 (and_12_out, not_1_out, not_2_out, C);
  and and_13 (and_13_out, not_1_out, C, not_4_out);
  and and_14 (and_14_out, not_2_out, not_3_out, not_4_out);
  and and_15 (and_15_out, not_1_out, B, not_3_out);
  and and_16 (and_16_out, not_1_out, B, not_4_out);
  or or_1 (out_5, and_1_out, and_2_out, and_3_out, and_4_out);
  or or_2 (out_9, and_5_out, and_6_out, and_7_out, and_8_out);
  or or_3 (out_18, and_7_out, and_9_out, and_10_out);
  or or_4 (out_23, and_3_out, and_11_out, and_12_out, and_13_out, and_14_out);
  or or_5 (out_17, and_13_out, and_14_out);
  or or_6 (out_8, and_3_out, and_8_out, and_15_out, and_16_out);
  or or_7 (out_14, and_15_out, and_3_out, and_12_out, and_13_out);

  assign out_6 = out_5;
  assign out_7 = out_5;
  assign out_10 = out_8;
  assign out_11 = out_9;
  assign out_12 = out_8;
  assign out_13 = out_9;
  assign out_15 = out_14;
  assign out_16 = out_14;
  assign out_19 = out_17;
  assign out_20 = out_18;
  assign out_21 = out_17;
  assign out_22 = out_18;
  assign out_24 = out_23;
  assign out_25 = out_23;

  // Notes on the sheet:
  //   A'C
  //   A'BD
  //   AB'C'
  //   A'B'D'
  //   A'B'
  //   A'CD
  //   B'C'
  //   A'C'D'
  //   A'D
  //   A'B
  //   A'BC'D
  //   A'B'C
  //   A'CD'
  //   B'C'D'
  //   A'BC'
  //   A'BD'
endmodule
