// Logisim project HW3#2a.circ as structural Verilog: 1 circuit, main circuit main
module main (
  input  A,
  input  B,
  input  C,
  input  D,
  output out_5
);

  wire not_1_out, not_2_out, w_out, x_out, y_out, z_out;

  not not_1 (not_1_out, A);
  not not_2 (not_2_out, D);
  or x (x_out, not_2_out, B, C);
  and y (y_out, not_1_out, C);
  and z (z_out, y_out, A);
  or F (out_5, x_out, w_out);
  and w (w_out, z_out, B);
endmodule
