// Logisim project HW3#2b.circ as structural Verilog: 1 circuit, main circuit main
module main (
  input  A0,
  input  A1,
  input  B0,
  input  B1,
  output out_5,
  output out_6,
  output out_7
);

  wire not_1_out, not_2_out, w1_out, w2_out, w3_out, xnor_1_out, xor_1_out;

  xor xor_1 (xor_1_out, A1, B1);
  xnor xnor_1 (xnor_1_out, A0, B0);
  not not_1 (not_1_out, A1);
  not not_2 (not_2_out, A0);
  and w1 (w1_out, not_1_out, B1);
  or w2 (w2_out, not_2_out, not_1_out, B0);
  and w3 (w3_out, not_2_out, B0, B1);
  and F3 (out_5, xor_1_out, xnor_1_out);
  or F2 (out_7, w1_out, w2_out, w3_out);
  nor F1 (out_6, out_5, out_7);

  // Notes on the sheet:
  //   w4
  //   w5
  //   w6
  //   w7
endmodule
