// Logisim project HW4.circ as structural Verilog: 1 circuit, main circuit main
module main (
  input  in_1,
  input  in_2,
  input  in_3,
  input  in_4,
  output out_5,
  output out_6,
  output out_7
);

  wire and_1_out, and_2_out, and_3_out, and_4_out, and_5_out, j_k_ff_1_qn, j_k_ff_2_qn, j_k_ff_3_qn,
       not_1_out, or_1_out, or_2_out, or_3_out, or_4_out;

  J_K_Flip_Flop j_k_ff_1 (
    .J(or_2_out), .clk(in_1), .K(in_1), .Q(out_5), .Qn(j_k_ff_1_qn), .en(in_3), .reset(in_2));  // open: preset
  J_K_Flip_Flop j_k_ff_2 (
    .J(or_1_out), .clk(in_1), .K(in_4), .Q(out_6), .Qn(j_k_ff_2_qn), .en(in_3), .reset(in_2));  // open: preset
  not not_1 (not_1_out, in_4);
  J_K_Flip_Flop j_k_ff_3 (
    .J(or_4_out), .clk(in_1), .K(or_3_out), .Q(out_7), .Qn(j_k_ff_3_qn), .en(in_3));  // open: preset, reset
  or or_1 (or_1_out, out_5, and_1_out);
  and and_1 (and_1_out, in_4, j_k_ff_3_qn);
  and and_2 (and_2_out, out_7, in_4, j_k_ff_2_qn);
  or or_2 (or_2_out, and_2_out, and_3_out);
  and and_3 (and_3_out, j_k_ff_2_qn, j_k_ff_3_qn, not_1_out);
  and and_4 (and_4_out, j_k_ff_1_qn, in_4, j_k_ff_2_qn);
  and and_5 (and_5_out, out_5, not_1_out);
  or or_3 (or_3_out, out_6, not_1_out);
  or or_4 (or_4_out, and_4_out, out_7, and_5_out);
endmodule
