// Logisim project HW4.circ as structural Verilog: 1 circuit, main circuit main
module main (
  input  in_1,
  input  in_2,
  input  in_3,
  input  in_4,
  output out_5,
  output out_6,
  output out_7
);

  wire and_1_out, and_2_out, and_3_out, and_4_out, and_5_out, and_6_out, and_7_out, and_8_out, and_9_out,
       and_10_out, and_11_out, and_12_out, and_13_out, and_14_out, and_15_out, and_16_out, j_k_ff_1_qn,
       j_k_ff_2_qn, j_k_ff_3_qn, not_1_out, or_1_out, or_2_out, or_3_out, or_4_out, or_5_out, or_6_out;

  and and_1 (and_1_out, j_k_ff_3_qn, j_k_ff_2_qn, not_1_out);
  not not_1 (not_1_out, in_4);
  and and_2 (and_2_out, out_6, j_k_ff_3_qn, in_4);
  or or_1 (or_1_out, and_2_out, and_1_out);
  J_K_Flip_Flop j_k_ff_1 (
    .J(or_1_out), .clk(in_1), .K(or_2_out), .Q(out_5), .Qn(j_k_ff_1_qn), .en(in_3), .reset(in_2));  // open: preset
  J_K_Flip_Flop j_k_ff_2 (
    .J(or_4_out), .clk(in_1), .K(or_3_out), .Q(out_6), .Qn(j_k_ff_2_qn), .en(in_3), .reset(in_2));  // open: preset
  J_K_Flip_Flop j_k_ff_3 (
    .J(or_5_out), .clk(in_1), .K(or_6_out), .Q(out_7), .Qn(j_k_ff_3_qn), .en(in_3), .reset(in_2));  // open: preset
  and and_3 (and_3_out, out_6, j_k_ff_3_qn, not_1_out);
  and and_4 (and_4_out, j_k_ff_2_qn, j_k_ff_3_qn, in_4);
  and and_5 (and_5_out, j_k_ff_1_qn, out_7, not_1_out);
  and and_6 (and_6_out, out_5, out_7, in_4);
  or or_2 (or_2_out, and_3_out, and_4_out);
  or or_3 (or_3_out, and_5_out, and_6_out);
  and and_7 (and_7_out, j_k_ff_1_qn, j_k_ff_2_qn, in_4);
  and and_8 (and_8_out, j_k_ff_1_qn, out_6, not_1_out);
  and and_9 (and_9_out, out_5, out_6, not_1_out);
  and and_10 (and_10_out, out_5, j_k_ff_2_qn, not_1_out);
  and and_11 (and_11_out, out_5, out_7, not_1_out);
  or or_4 (or_4_out, and_11_out, and_12_out);
  and and_12 (and_12_out, out_7, in_4, j_k_ff_1_qn);
  or or_5 (or_5_out, and_7_out, and_8_out, and_9_out, and_10_out);
  and and_13 (and_13_out, j_k_ff_1_qn, j_k_ff_2_qn, not_1_out);
  and and_14 (and_14_out, j_k_ff_1_qn, j_k_ff_2_qn, not_1_out);
  and and_15 (and_15_out, out_5, out_6, not_1_out);
  and and_16 (and_16_out, out_5, j_k_ff_2_qn, in_4);
  or or_6 (or_6_out, and_13_out, and_14_out, and_15_out, and_16_out);
endmodule
